# Fritzing sketch Esquematico (saved by Fritzing 0.9.2b)
circuit board: 8.46667cm x 5.64444cm
breadboards: 1

parts:
  Adafruit_HUZZAH_ESP8266_Breakout1 = Adafruit HUZZAH ESP8266 Breakout [part_number=2471]
  U1 = LM 358 Dual Op-Amp [package="DIP8 [THT]"]
  Q1 = LTR-301 [package=ltr-301]
  D1 = LTE-302 [package=lte-302]
  Q2 = LTR-301 [package=ltr-301]
  D2 = LTE-302 [package=lte-302]
  R1 = Resistor [tolerance=±5% resistance=10k package="1206 [SMD]"]
  R2 = Resistor [tolerance=±5% resistance=10k package="1206 [SMD]"]
  R3 = Resistor [tolerance=±5% resistance=10k package="1206 [SMD]"]
  R4 = Resistor [tolerance=±5% resistance=10k package="1206 [SMD]"]
  R5 = Resistor [tolerance=±5% resistance=4.7k package="1206 [SMD]"]
  R6 = Resistor [tolerance=±5% resistance=4.7k package="1206 [SMD]"]
  R7 = Resistor [tolerance=±5% resistance=10k package="1206 [SMD]"]
  Q3 = TRANSISTOR_NPN [package=to-92]

nets:
  N1: Adafruit_HUZZAH_ESP8266_Breakout1.GND, Q1.E, Q2.E, R3.Pin_1
  N2: Adafruit_HUZZAH_ESP8266_Breakout1.#13, U1.connector6, R6.Pin_0
  N3: Adafruit_HUZZAH_ESP8266_Breakout1.#5, Q3.B
  N4: Adafruit_HUZZAH_ESP8266_Breakout1.#4, U1.connector0, R5.Pin_0
  N5: Adafruit_HUZZAH_ESP8266_Breakout1.3V, U1.connector3, R2.Pin_1, R5.Pin_1, R7.Pin_1
  N6: U1.connector1, Q1.C
  N7: U1.connector2, R3.Pin_0, R7.Pin_0
  N8: U1.connector4, R1.Pin_1, R4.Pin_1
  N9: U1.connector5, Q2.C, R2.Pin_0
  N10: U1.connector7, D1.A, D2.A, R1.Pin_0
  N11: D1.C, D2.C, Q3.C
  N12: R4.Pin_0, R6.Pin_1, Q3.E
